# Fritzing sketch Shema (saved by Fritzing 1.0.5)
breadboards: 1

parts:
  T1 = LM35 Temperature Sensor [package="TO92 [THT]"]
  BATT1 = 4xAA Switchable Battery Pack w/Bare Wire
  WeMos_D1_Mini_Relay_Shield_V1 = WeMos D1 Mini Relay Shield V2
  IC1 = 2.8 inch LCD SPI display with touch screen & SD card
  Mod1 = KY-026 Flame Sensor Module [package="Breakout board"]
  Mod2 = Raspberry Pi Pico
  WATER_PUMP1 = water pump/motor  # not connected

nets:
  N1: T1.+Vs, IC1.pin2, IC1.pin8, Mod1.+, Mod2.pin_36
  N2: T1.Vout, Mod2.pin_31
  N3: T1.GND, BATT1.POS, WeMos_D1_Mini_Relay_Shield_V1.G, IC1.pin1, Mod1.G, Mod2.pin_3, Mod2.pin_8, Mod2.pin_23, Mod2.pin_28, Mod2.pin_42
  N4: BATT1.NEG, WeMos_D1_Mini_Relay_Shield_V1.COM
  N5: WeMos_D1_Mini_Relay_Shield_V1.5V, Mod2.pin_40
  N6: WeMos_D1_Mini_Relay_Shield_V1.D1, Mod2.pin_17
  N7: IC1.pin3, Mod2.pin_22
  N8: IC1.pin4, Mod2.pin_21
  N9: IC1.pin5, Mod2.pin_20
  N10: IC1.pin6, Mod2.pin_25
  N11: IC1.pin7, Mod2.pin_24
  N12: Mod1.D0, Mod2.pin_19

notes:
  pico
  Banggood TFT displej
  LM35
  Senzor plamena
  Relej
  Pumpa

custom parts:
  4xAA Switchable Battery Pack w/Bare Wire: 4xAA Switchable Battery Pack with Bare Wire connection
  2.8 inch LCD SPI display with touch screen & SD card: A generic 2.8 inch LCD TFT 320x280 display with touchscreen and SD card slot.
  KY-026 Flame Sensor Module: KY-026 Flame Sensor Module reacts in the presence of fire.
  Raspberry Pi Pico: Raspberry Pi Pico. Based around the RP2040 microcontroller the Pico is a low cost microcontroller device bringing Raspberry Pi quality, cost, and easy of use to the microcontroller space. Jan 2021, Split part in to two versions: tht (this one) and SMD. This one will drill holes for a .1 in header in pcb to allow plugging in the module as well as providing pads to solder the module to the top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
  water pump/motor: WATER PUMP BY ARDUBLOCKTR

// code stored in the sketch: shema.ino

